// Digital circuit atk16_mem.dig as structural Verilog
module atk16_mem (
  input  [15:0] ADDR,
  input  [15:0] DBUS,
  input  MEM_IE,
  input  MEM_OE
);

  wire [14:0] demultiplexer_1_out_0, demultiplexer_1_out_1;
  wire [15:0] driverinvsel_1_out, MEM_RAM_q, MEM_ROM_d;

  Demultiplexer #(.Bits(15)) demultiplexer_1 (
    .sel(ADDR[15]), .in(ADDR[14:0]), .out_0(demultiplexer_1_out_0), .out_1(demultiplexer_1_out_1));
  RAMAsync #(.AddrBits(15), .Bits(16)) MEM_RAM (.A(demultiplexer_1_out_1), .D(DBUS), .we(MEM_IE), .Q(MEM_RAM_q));
  assign DBUS = MEM_OE ? driverinvsel_1_out : 16'bz;  // Driver driver_1
  EEPROM #(.AddrBits(15), .isProgramMemory("true"), .Bits(16)) MEM_ROM (
    .A(demultiplexer_1_out_0), .CS(1'b1), .WE(1'b0), .OE(1'b1), .D(MEM_ROM_d));
  assign driverinvsel_1_out = ~ADDR[15] ? MEM_ROM_d : 16'bz;  // DriverInvSel driverinvsel_1
  assign driverinvsel_1_out = ADDR[15] ? MEM_RAM_q : 16'bz;  // Driver driver_2
  // Probe ROM_OUT on MEM_ROM_d
  // Probe RAM_OUT on MEM_RAM_q

  // Notes on the sheet:
  //   ADDR: Address
  //   DBUS: Data bus
  //   MEM_IE: Memory input enable
  //   MEM_OE: Memory output enable
  //   contents of MEM_ROM (hex, n*v repeats v):
  //   420a,9c00,3dc0,1fc8,6004,f000,35c0,1fc8,37c0,1fc8,4602,259,8609
  //   ,39c0,1fc8,3bc0,1fc8,4a01,4400,4601,898,14c0,1700,269,8400,5ff6
  //   ,1fc9,27c0,1fc9,25c0,1fc9,2dc0,5180,2840,1fc9,2bc0,1fc9,29c0,1fc9
  //   ,27c0,1fc9,25c0,1fc9,2dc0,5180
endmodule

/* Test case:
ADDR   MEM_IE  MEM_OE   DBUS  DBUS_out

# read ROM
program(0xFF)
0x0    0       1        Z      0xFF

# read RAM
memory MEM_RAM(0x0)=0x55;
0      0       0        Z      X
0x8000 0       1        Z      0x55

# write to RAM
0x8000 1       0        0xAA   0xAA
0x8000 0       1        Z      0xAA
*/
