// Digital circuit atk16_tpu.dig as structural Verilog
module atk16_tpu (
  input  MMIO_IE,
  input  MMIO_OE,
  input  [12:0] MMIO_S,
  input  PCLK,
  input  CLK,
  input  [15:0] DBUS,
  input  [8:0] X,
  input  [7:0] Y,
  output [1:0] PR,
  output [1:0] PG,
  output [1:0] PB
);

  wire COVF, MMIOMATCH, not_1_out;
  wire [2:0] CX;
  wire [5:0] TX;
  wire [7:0] CHAR_S, CHARMEM_d;
  wire [10:0] multiplexer_1_out;

  and and_1 (MMIOMATCH, MMIO_S[11], MMIO_S[12], MMIO_IE);
  Multiplexer #(.Bits(11)) multiplexer_1 (
    .sel(MMIOMATCH), .in_0({TX, Y[7:3]}), .in_1(MMIO_S[10:0]), .out(multiplexer_1_out));
  not not_1 (not_1_out, COVF);
  RAMDualPort #(.AddrBits(11), .Bits(8)) TEXTMEM (
    .A(multiplexer_1_out), .Din(DBUS[7:0]), .str(MMIOMATCH), .C(not_1_out), .ld(1'b1), .D(CHAR_S));
  Counter #(.Bits(3)) counter_1 (.en(1'b1), .C(PCLK), .clr(1'b0), .out(CX), .ovf(COVF));
  Counter #(.Bits(6)) counter_2 (.en(1'b1), .C(COVF), .clr(1'b0), .out(TX));  // open: ovf
  // Probe on CHAR_S
  EEPROM #(.AddrBits(11), .Bits(8)) CHARMEM (.A({CHAR_S, Y[2:0]}), .CS(1'b1), .WE(1'b0), .OE(1'b1), .D(CHARMEM_d));
  // Probe on CHARMEM_d
  BitSelector #(.Selector_Bits(3)) bitselector_1 (.in(CHARMEM_d), .sel(CX), .out(PB[1]));
  // Probe on CX
  // Probe on PB[1]

  assign PB[0] = PB[1];
  assign PG = {2{PB[1]}};
  assign PR = {2{PB[1]}};

  // Other names for the same wires on the sheet: CCOLOR = PB[1]; DBUS_L8[7:0] = DBUS[7:0];
  //   MMIOADDR[10:0] = MMIO_S[10:0]; CY[2:0] = Y[2:0]; TY[4:0] = Y[7:3]

  // Notes on the sheet:
  //   MMIO_S: MMI/O selector
  //   PCLK: Pixel clock
  //   CLK: CPU clock
  //   DBUS: Data bus
  //   X: X pixel
  //   Y: Y pixel
  //   contents of CHARMEM (hex, n*v repeats v):
  //   c,1e,33,33,3f,33,33,0,3f,66,66,3e,66,66,3f,0,3c,66,3,3,3,66,3c
  //   ,0,1f,36,66,66,66,36,1f,0,7f,46,16,1e,16,46,7f,0,7f,46,16,1e,16
  //   ,6,f,0,3c,66,3,3,73,66,7c,0,33,33,33,3f,33,33,33,0,1e,5*c,1e
endmodule
